// Logisim project 8bitRegister.circ as structural Verilog: 1 circuit, main circuit 8bitReg
module _8bitReg (
  input  Up_nDown,
  input  Load,
  input  [7:0] Din,
  input  Clk,
  input  nCarryIn,
  input  Reset,
  output Zero,
  output [7:0] Dout
);

  wire and_1_out, nor_1_out, not_1_out, not_2_out, or_1_out, or_2_out;

  not not_1 (not_1_out, Up_nDown);
  not not_2 (not_2_out, Load);
  and and_1 (and_1_out, Clk, ~nCarryIn);  // AND_Gate
  or or_1 (or_1_out, not_1_out, Load);
  Counter counter_1 (
    .load(or_1_out), .D(Din), .count(not_2_out), .Q(Dout), .clk(or_2_out), .clr(Reset));  // open: carry
  or or_2 (or_2_out, Load, and_1_out);
  nor nor_1 (nor_1_out, Dout[0], Dout[1], Dout[2], Dout[3], Dout[5], Dout[6], Dout[7], Dout[4]);
  and and_2 (Zero, nor_1_out, ~nCarryIn);  // AND_Gate

  // Notes on the sheet:
  //   Trying to make Logisim Counter function similar to CD4516B
endmodule
