// Logisim project CD4516B.circ as structural Verilog: 1 circuit, main circuit CD4516BE
module CD4516BE (
  input  P0,
  input  P1,
  input  P2,
  input  P3,
  input  Reset,
  input  Preset_Enable,
  input  Clock,
  input  nCarryIn,
  input  Up_Down,
  input  VCC,
  input  VSS,
  output Q0,
  output Q1,
  output Q2,
  output Q3,
  output nCarryOut
);

  wire and_1_out, and_2_out, and_3_out, and_4_out, and_5_out, and_6_out, and_7_out, and_8_out, and_9_out,
       and_10_out, and_11_out, d_ff_2_qn, d_ff_3_qn, d_ff_4_qn, nand_1_out, nand_3_out, nand_4_out,
       nand_5_out, nand_6_out, nand_7_out, nand_8_out, nand_9_out, nand_10_out, nand_11_out, nand_12_out,
       nand_13_out, nand_14_out, or_1_out, or_2_out, xnor_1_out, xor_1_out, xor_2_out, xor_3_out, xor_4_out;

  nand nand_1 (nand_1_out, ~Reset, P0);  // NAND_Gate
  or or_1 (or_1_out, Reset, Preset_Enable);
  or or_2 (or_2_out, Preset_Enable, Reset, Clock);
  nand nand_2 (nCarryOut, nand_4_out, xnor_1_out, ~nCarryIn);  // NAND_Gate
  xnor xnor_1 (xnor_1_out, Up_Down, Q0);
  xor xor_1 (xor_1_out, Q0, ~nCarryIn);  // XOR_Gate
  and and_1 (and_1_out, ~nand_1_out, or_1_out);  // AND_Gate
  and and_2 (and_2_out, nand_1_out, or_1_out);
  nand nand_3 (nand_3_out, Up_Down, Q1, Q2, Q3);
  D_Flip_Flop d_ff_1 (.clk(or_2_out), .D(xor_1_out), .Q(Q0), .preset(and_1_out), .reset(and_2_out));  // open: Qn, en
  and and_3 (and_3_out, ~nCarryIn, xnor_1_out);  // AND_Gate
  nand nand_4 (nand_4_out, nand_3_out, nand_5_out);
  nand nand_5 (nand_5_out, ~Up_Down, d_ff_2_qn, d_ff_3_qn, d_ff_4_qn);  // NAND_Gate
  nand nand_6 (nand_6_out, ~Reset, P1);  // NAND_Gate
  D_Flip_Flop d_ff_2 (
    .clk(or_2_out), .D(xor_2_out), .Q(Q1), .Qn(d_ff_2_qn), .preset(and_5_out), .reset(and_4_out));  // open: en
  xor xor_2 (xor_2_out, Q1, and_3_out);
  and and_4 (and_4_out, nand_6_out, or_1_out);
  and and_5 (and_5_out, ~nand_6_out, or_1_out);  // AND_Gate
  and and_6 (and_6_out, ~nCarryIn, xnor_1_out, nand_7_out);  // AND_Gate
  nand nand_7 (nand_7_out, nand_8_out, nand_10_out);
  nand nand_8 (nand_8_out, Up_Down, Q1);
  nand nand_9 (nand_9_out, ~Reset, P2);  // NAND_Gate
  D_Flip_Flop d_ff_3 (
    .clk(or_2_out), .D(xor_3_out), .Q(Q2), .Qn(d_ff_3_qn), .preset(and_8_out), .reset(and_7_out));  // open: en
  xor xor_3 (xor_3_out, Q2, and_6_out);
  and and_7 (and_7_out, nand_9_out, or_1_out);
  and and_8 (and_8_out, ~nand_9_out, or_1_out);  // AND_Gate
  nand nand_10 (nand_10_out, ~Up_Down, d_ff_2_qn);  // NAND_Gate
  and and_9 (and_9_out, ~nCarryIn, xnor_1_out, nand_11_out);  // AND_Gate
  nand nand_11 (nand_11_out, nand_12_out, nand_14_out);
  nand nand_12 (nand_12_out, Up_Down, Q1, Q2);
  nand nand_13 (nand_13_out, ~Reset, P3);  // NAND_Gate
  D_Flip_Flop d_ff_4 (
    .clk(or_2_out), .D(xor_4_out), .Q(Q3), .Qn(d_ff_4_qn), .preset(and_11_out), .reset(and_10_out));  // open: en
  xor xor_4 (xor_4_out, Q3, and_9_out);
  and and_10 (and_10_out, nand_13_out, or_1_out);
  and and_11 (and_11_out, ~nand_13_out, or_1_out);  // AND_Gate
  nand nand_14 (nand_14_out, ~Up_Down, d_ff_2_qn, d_ff_3_qn);  // NAND_Gate
endmodule
