// Logisim project CPU.circ as structural Verilog: 7 circuits, main circuit main
module main (
  input  in_1
);

  wire ACCena, ACCload, and_1_out, and_2_out, and_4_out, and_5_out, and_6_out, Bus1, Clk, Clk_t, clock_1_out,
       DI_nCnt, DIena, DIload, Fena, Fload, Had_nda, Hadda_nOE, hm62256sel_1_load, hm62256sel_1_sel, INTdis,
       INTena, IRload, IRQjmp, LaddaOE, lTMPena, lTMPload, MAR_nCnt, MARload, MEM_ne, MEM_ns, nand_1_out,
       not_2_out, not_3_out, not_4_out, or_1_out, or_2_out, PC_nCnt, PCena, PCload, RAena, RAload, RBena,
       RBload, RCena, RCload, RDena, RDload, romsel_1_romh, romsel_1_roml, Rst, SI_nCnt, SIena, SIload,
       SP_nCnt, SPena, SPload, StpRst, TMPload, U_nD;
  wire [2:0] ALUop, n8bitreg_3_dout_2;
  wire [3:0] alu_1_flags, Flags;
  wire [7:0] alu_1_res, bus1_1_out_3, controlled_buffer_1_out, controlled_buffer_1_out_2,
       controlled_buffer_5_out, n8bitreg_1_dout, n8bitreg_2_dout, n8bitreg_2_dout_2, n8bitreg_3_dout,
       n8bitreg_4_dout, n8bitreg_5_dout, n8bitreg_6_dout, n8bitreg_7_dout, n8bitreg_8_dout,
       n8bitreg_8_dout_2, n8bitreg_9_dout, n8bitreg_10_dout, pull_resistor_1_node;
  wire [7:3] n8bitreg_3_dout_2_2;
  wire [7:4] n8bitreg_10_dout_2, pull_resistor_3_node;
  wire [15:0] n16bitreg_1_dout, n16bitreg_2_dout, n16bitreg_3_dout, n16bitreg_4_dout, n16bitreg_5_dout,
       n16bitreg_5_dout_2;
  wire [15:15] interrupt_1_intout;

  Button button_1 (.out(Rst));
  Clock clock_1 (.out(clock_1_out));
  buf buffer_1 (Clk, clock_1_out);
  not not_1 (Clk_t, clock_1_out);
  not not_2 (not_2_out, Clk_t);
  assign {controlled_buffer_1_out_2, controlled_buffer_1_out} = IRQjmp ? 16'h3 : 16'bz;  // Controlled_Buffer controlled_buffer_1
  and and_1 (and_1_out, not_2_out, Clk_t);
  and and_2 (and_2_out, and_1_out, IRload);
  _8bitreg u_8bitreg_1 (
    .Load(lTMPload), .DataIn(pull_resistor_1_node), .nCntEna(1'b1), .Reset(Rst), .Up_nDown(1'b0),
    .Enable(lTMPena), .Dout(n8bitreg_1_dout), .Dout_2(controlled_buffer_1_out));  // open: Clock, Zout
  Pull_Resistor pull_resistor_1 (.node(pull_resistor_1_node));
  _8bitreg u_8bitreg_2 (
    .Load(and_2_out), .DataIn(pull_resistor_1_node), .nCntEna(1'b1), .Reset(Rst), .Up_nDown(1'b0),
    .Enable(1'b1), .Dout(n8bitreg_2_dout), .Dout_2({n8bitreg_2_dout_2[7], ALUop, n8bitreg_2_dout_2[3:0]}));  // open: Clock, Zout
  // Probe on n8bitreg_2_dout
  ROM #(.addrWidth(16)) rom_1 (
    .addr({interrupt_1_intout[15], Flags, n8bitreg_2_dout_2[7], ALUop, n8bitreg_2_dout_2[3:0], n8bitreg_3_dout_2}),
    .data({lTMPload, DIload, SIload, SPload, PCload, MARload, MEM_ns, IRload}));  // open: sel
  ROM #(.addrWidth(16)) rom_2 (
    .addr({interrupt_1_intout[15], Flags, n8bitreg_2_dout_2[7], ALUop, n8bitreg_2_dout_2[3:0], n8bitreg_3_dout_2}),
    .data({Bus1, Fload, ACCload, TMPload, RDload, RCload, RBload, RAload}));  // open: sel
  // Probe on n8bitreg_1_dout
  or or_1 (or_1_out, n8bitreg_3_dout_2_2[3], StpRst, Rst);
  _16bitreg u_16bitreg_1 (
    .DataIn({controlled_buffer_1_out_2, controlled_buffer_1_out}), .Clock(Clk_t), .Load(SPload),
    .nCntEna(SP_nCnt), .Up_nDown(U_nD), .Reset(Rst), .Enable(SPena), .Dout(n16bitreg_1_dout),
    .Dout_2({controlled_buffer_1_out_2, controlled_buffer_1_out}));
  _8bitreg u_8bitreg_3 (
    .Load(1'b0), .Clock(Clk_t), .nCntEna(1'b0), .Reset(or_1_out), .Up_nDown(1'b1), .Enable(1'b1),
    .Dout(n8bitreg_3_dout), .Dout_2({n8bitreg_3_dout_2_2, n8bitreg_3_dout_2}));  // open: DataIn, Zout
  // Probe on n8bitreg_3_dout
  Interrupt interrupt_1 (
    .INTcatch(or_1_out), .INT(in_1), .INTdis(INTdis), .Rst(Rst), .INTena(INTena),
    .INTout(interrupt_1_intout[15]));
  // Probe on n16bitreg_1_dout
  _16bitreg u_16bitreg_2 (
    .DataIn({controlled_buffer_1_out_2, controlled_buffer_1_out}), .Clock(Clk_t), .Load(PCload),
    .nCntEna(PC_nCnt), .Up_nDown(U_nD), .Reset(Rst), .Enable(PCena), .Dout(n16bitreg_2_dout),
    .Dout_2({controlled_buffer_1_out_2, controlled_buffer_1_out}));
  // Probe on n16bitreg_2_dout
  _8bitreg u_8bitreg_4 (
    .Load(RAload), .DataIn(pull_resistor_1_node), .nCntEna(1'b1), .Reset(Rst), .Up_nDown(1'b0),
    .Enable(RAena), .Dout(n8bitreg_4_dout), .Dout_2(pull_resistor_1_node));  // open: Clock, Zout
  // Probe on n8bitreg_4_dout
  and and_3 (IRQjmp, lTMPload, Had_nda);
  _8bitreg u_8bitreg_5 (
    .Load(RBload), .DataIn(pull_resistor_1_node), .nCntEna(1'b1), .Reset(Rst), .Up_nDown(1'b0),
    .Enable(RBena), .Dout(n8bitreg_5_dout), .Dout_2(pull_resistor_1_node));  // open: Clock, Zout
  // Probe on n8bitreg_5_dout
  ROM #(.addrWidth(16)) rom_3 (
    .addr({interrupt_1_intout[15], Flags, n8bitreg_2_dout_2[7], ALUop, n8bitreg_2_dout_2[3:0], n8bitreg_3_dout_2}),
    .data({lTMPena, DIena, SIena, SPena, PCena, StpRst, MEM_ne, U_nD}));  // open: sel
  ROM #(.addrWidth(16)) rom_4 (
    .addr({interrupt_1_intout[15], Flags, n8bitreg_2_dout_2[7], ALUop, n8bitreg_2_dout_2[3:0], n8bitreg_3_dout_2}),
    .data({INTdis, INTena, Fena, ACCena, RDena, RCena, RBena, RAena}));  // open: sel
  // Probe on n16bitreg_3_dout
  _16bitreg u_16bitreg_3 (
    .DataIn({controlled_buffer_1_out_2, controlled_buffer_1_out}), .Clock(Clk_t), .Load(DIload),
    .nCntEna(DI_nCnt), .Up_nDown(U_nD), .Reset(Rst), .Enable(DIena), .Dout(n16bitreg_3_dout),
    .Dout_2({controlled_buffer_1_out_2, controlled_buffer_1_out}));
  _8bitreg u_8bitreg_6 (
    .Load(RCload), .DataIn(pull_resistor_1_node), .nCntEna(1'b1), .Reset(Rst), .Up_nDown(1'b0),
    .Enable(RCena), .Dout(n8bitreg_6_dout), .Dout_2(pull_resistor_1_node));  // open: Clock, Zout
  _16bitreg u_16bitreg_4 (
    .DataIn({controlled_buffer_1_out_2, controlled_buffer_1_out}), .Clock(Clk_t), .Load(SIload),
    .nCntEna(SI_nCnt), .Up_nDown(U_nD), .Reset(Rst), .Enable(SIena), .Dout(n16bitreg_4_dout),
    .Dout_2({controlled_buffer_1_out_2, controlled_buffer_1_out}));
  // Probe on n8bitreg_6_dout
  // Probe on n16bitreg_4_dout
  Pull_Resistor pull_resistor_2 (.node({controlled_buffer_1_out_2, controlled_buffer_1_out}));
  _8bitreg u_8bitreg_7 (
    .Load(RDload), .DataIn(pull_resistor_1_node), .nCntEna(1'b1), .Reset(Rst), .Up_nDown(1'b0),
    .Enable(RDena), .Dout(n8bitreg_7_dout), .Dout_2(pull_resistor_1_node));  // open: Clock, Zout
  // Probe on n8bitreg_7_dout
  and and_4 (and_4_out, Had_nda, ~Hadda_nOE);  // AND_Gate
  assign pull_resistor_1_node = and_4_out ? controlled_buffer_1_out_2 : 8'bz;  // Controlled_Buffer controlled_buffer_2
  assign controlled_buffer_1_out_2 = and_5_out ? pull_resistor_1_node : 8'bz;  // Controlled_Buffer controlled_buffer_3
  assign pull_resistor_1_node = LaddaOE ? controlled_buffer_1_out : 8'bz;  // Controlled_Buffer controlled_buffer_4
  // Probe on pull_resistor_1_node
  _8bitreg u_8bitreg_8 (
    .Load(TMPload), .DataIn(pull_resistor_1_node), .nCntEna(1'b1), .Reset(Rst), .Up_nDown(1'b0),
    .Enable(1'b1), .Dout(n8bitreg_8_dout), .Dout_2(n8bitreg_8_dout_2));  // open: Clock, Zout
  // Probe on n8bitreg_8_dout
  Bus1 bus1_1 (.in_1(n8bitreg_8_dout_2), .in_2(Bus1), .out_3(bus1_1_out_3));
  ROM #(.addrWidth(16)) rom_5 (
    .addr({interrupt_1_intout[15], Flags, n8bitreg_2_dout_2[7], ALUop, n8bitreg_2_dout_2[3:0], n8bitreg_3_dout_2}),
    .data({Had_nda, Hadda_nOE, LaddaOE, DI_nCnt, SI_nCnt, PC_nCnt, SP_nCnt, MAR_nCnt}));  // open: sel
  and and_5 (and_5_out, ~Had_nda, ~Hadda_nOE);  // AND_Gate
  // Probe on {controlled_buffer_1_out_2, controlled_buffer_1_out}
  and and_6 (and_6_out, ~Bus1, Flags[0]);  // AND_Gate
  ALU alu_1 (
    .Cin(and_6_out), .A(pull_resistor_1_node), .B(bus1_1_out_3), .Operation(ALUop), .Flags(alu_1_flags),
    .Res(alu_1_res));
  Pull_Resistor pull_resistor_3 (.node({pull_resistor_3_node, alu_1_flags}));
  _8bitreg u_8bitreg_9 (
    .Load(ACCload), .DataIn(alu_1_res), .nCntEna(1'b1), .Reset(Rst), .Up_nDown(1'b0), .Enable(ACCena),
    .Dout(n8bitreg_9_dout), .Dout_2(pull_resistor_1_node));  // open: Clock, Zout
  _16bitreg u_16bitreg_5 (
    .DataIn({controlled_buffer_1_out_2, controlled_buffer_1_out}), .Clock(Clk_t), .Load(MARload),
    .nCntEna(MAR_nCnt), .Up_nDown(U_nD), .Reset(Rst), .Enable(1'b1), .Dout(n16bitreg_5_dout),
    .Dout_2(n16bitreg_5_dout_2));
  // Probe on n16bitreg_5_dout
  assign controlled_buffer_5_out = Fload ? pull_resistor_1_node : 8'bz;  // Controlled_Buffer controlled_buffer_5
  assign controlled_buffer_5_out = ACCload ? {pull_resistor_3_node, alu_1_flags} : 8'bz;  // Controlled_Buffer controlled_buffer_6
  or or_2 (or_2_out, Fload, ACCload);
  // Probe on n8bitreg_9_dout
  _8bitreg u_8bitreg_10 (
    .Load(or_2_out), .DataIn(controlled_buffer_5_out), .nCntEna(1'b1), .Reset(Rst), .Up_nDown(1'b0),
    .Enable(1'b1), .Dout(n8bitreg_10_dout), .Dout_2({n8bitreg_10_dout_2, Flags}));  // open: Clock, Zout
  // Probe on n8bitreg_10_dout
  assign pull_resistor_1_node = Fena ? {n8bitreg_10_dout_2, Flags} : 8'bz;  // Controlled_Buffer controlled_buffer_7
  nand nand_1 (nand_1_out, n16bitreg_5_dout_2[15], Clk);
  ROMsel romsel_1 (.MEM_ne(MEM_ne), .Addr(n16bitreg_5_dout_2), .ROMh(romsel_1_romh), .ROMl(romsel_1_roml));
  HM62256sel hm62256sel_1 (
    .nWE(MEM_ns), .nCE(nand_1_out), .nOE(MEM_ne), .Sel(hm62256sel_1_sel), .Load(hm62256sel_1_load));
  not not_3 (not_3_out, romsel_1_romh);
  not not_4 (not_4_out, romsel_1_roml);
  RAM #(.addrWidth(15), .bus("asynch")) ram_1 (
    .addr(n16bitreg_5_dout_2[14:0]), .data(pull_resistor_1_node), .sel(hm62256sel_1_sel),
    .ld(hm62256sel_1_load));  // open: clr
  ROM #(.addrWidth(13)) rom_6 (.addr(n16bitreg_5_dout_2[12:0]), .data(pull_resistor_1_node), .sel(not_3_out));
  ROM #(.addrWidth(13)) rom_7 (.addr(n16bitreg_5_dout_2[12:0]), .data(pull_resistor_1_node), .sel(not_4_out));

  // Other names for the same wires on the sheet: INT = in_1

  // Notes on the sheet:
  //   lTMP
  //   IR
  //   uCode2
  //   contents of rom_1 (hex, n*v repeats v):
  //   3 7*2 3 7*2 3 7*2 3 7*2 3 7*2 3 7*2 3 7*2 3 7*2 3 7*2 3 7*2 3 7*2 3 7*2 3 7*2 3 7*2 3 7*2 3 7*2 3
  //   7*2 3 7*2 3 7*2 3 7*2 3 7*2 3 7*2 3 7*2 3 7*2 3 7*2 3 7*2 3 7*2 3 7*2 3 7*2 3 7*2 3 7*2 3 7*2 3 7*2
  //   3 7*2 3 7*2 3 7*2 3 7*2 3 7*2 3 7*2 3 7*2 3 7*2 3 7*2 3 7*2 3 7*2 3 7*2 3 7*2 3 7*2 3 7*2 3 7*2 3
  //   7*2 3 7*2 3 7*2 3 7*2 3 7*2 3 7*2 3 7*2 3 7*2 3 7*2 3 7*2 3 7*2 3 7*2 3 7*2 3 7*2 3 7*2 3 7*2 3 7*2
  //   3 7*2 3 7*2 3 7*2 3 7*2 3 7*2 3 7*2 3 7*2 3 7*2 3 7*2 3 7*2 3 7*2 3 7*2 3 7*2 3 7*2 3 7*2 3 7*2 3
  //   7*2 3 7*2 3 7*2 3 7*2 3 7*2 3 7*2 3 7*2 3 7*2 3 7*2 3 7*2 3 7*2 3 7*2 3 7*2 3 7*2 3 7*2 3 7*2 3 7*2
  //   3 7*2 3 7*2 3 7*2 3 7*2 3 7*2 3 7*2 3 7*2 3 7*2 3 7*2 3 7*2 3 7*2 3 7*2 3 7*2 3 7*2 3 7*2 3 7*2 3
  //   7*2 3 7*2 3 7*2 3 7*2 3 7*2 3 7*2 3 7*2 3 7*2 3 7*2 3 7*2 3 7*2 3 7*2 3 7*2 3 7*2 3 7*2 3 7*2 3 7*2
  //   3 7*2 3 7*2 3 7*2 3 7*2 3 7*2 3 7*2 3 7*2 3 7*2 3 7*2 3 7*2 3 7*2 3 7*2 3 7*2 3 7*2 3 7*2 3 7*2 3
  //   7*2 3 7*2 3 7*2 3 7*2 3 7*2 3 7*2 3 7*2 3 7*2 3 7*2 3 7*2 3 7*2 3 7*2 3 7*2 3 7*2 3 7*2 3 7*2 3 7*2
  //   3 7*2 3 7*2 3 7*2 3 7*2 3 7*2 3 7*2 3 7*2 3 7*2 3 7*2 3 7*2 3 7*2 3 7*2 3 7*2 3 7*2 3 7*2 3 7*2 3
  //   7*2 3 7*2 3 7*2 3 7*2 3 7*2 3 7*2 3 7*2 3 7*2 3 7*2 3 7*2 3 7*2 3 7*2 3 7*2 3 7*2 3 7*2 3 7*2 3 7*2
  //   3 7*2 3 7*2 3 7*2 3 7*2 3 7*2 3 7*2 3 7*2 3 7*2 3 7*2 3 7*2 3 7*2 3 7*2 3 7*2 3 7*2 3 7*2 3 7*2 3
  //   7*2 3 7*2 3 7*2 3 7*2 3 7*2 3 7*2 3 7*2 3 7*2 3 7*2 3 7*2 3 7*2 3 7*2 3 7*2 3 7*2 3 7*2 3 7*2 3 7*2
  //   3 7*2 3 7*2 3 7*2 3 7*2 3 7*2 3 7*2 3 7*2 3 7*2 3 7*2 3 7*2 3 7*2 3 7*2 3 7*2 3 7*2 3 7*2 3 7*2 3
  //   7*2 3 7*2 3 7*2 3 7*2 3 7*2 3 7*2 3 7*2 3 7*2 3 7*2 3 7*2 3 7*2 3 7*2 3 7*2 3 7*2 3 7*2 3 7*2 3 7*2
  //   3 7*2 3 7*2 3 7*2 3 7*2 3 7*2 3 7*2 3 7*2 3 7*2 3 7*2 3 7*2 3 7*2 3 7*2 3 7*2 3 7*2 3 7*2 3 7*2 3
  //   7*2 3 7*2 3 7*2 3 7*2 3 7*2 3 7*2 3 7*2 3 7*2 3 7*2 3 7*2 3 7*2 3 7*2 3 7*2 3 7*2 3 7*2 3 7*2 3 7*2
  //   3 7*2 3 7*2 3 7*2 3 7*2 3 7*2 3 7*2 3 7*2 3 7*2 3 7*2 3 7*2 3 7*2 3 7*2 3 7*2 3 7*2 3 7*2 3 7*2 3
  //   7*2 3 7*2 3 7*2 3 7*2 3 7*2 3 7*2 3 7*2 3 7*2 3 7*2 3 7*2 3 7*2 3 7*2 3 7*2 3 7*2 3 7*2 3 7*2 3 7*2
  //   3 7*2 3 7*2 3 7*2 3 7*2 3 7*2 3 7*2 3 7*2 3 7*2 3 7*2 3 7*2 3 7*2 3 7*2 3 7*2 3 7*2 3 7*2 3 7*2 3
  //   7*2 3 7*2 3 7*2 3 7*2 3 7*2 3 7*2 3 7*2 3 7*2 3 7*2 3 7*2 3 7*2 3 7*2 3 7*2 3 7*2 3 7*2 3 7*2 3 7*2
  //   3 7*2 3 7*2 3 7*2 3 7*2 3 7*2 3 7*2 3 7*2 3 7*2 3 7*2 3 7*2 3 7*2 3 7*2 3 7*2 3 7*2 3 7*2 3 7*2 3
  //   7*2 3 7*2 3 7*2 3 7*2 3 7*2 3 7*2 3 7*2 3 7*2 3 7*2 3 7*2 3 7*2 3 7*2 3 7*2 3 7*2 3 7*2 3 7*2 3 7*2
  //   3 7*2 3 7*2 3 7*2 3 7*2 3 7*2 3 7*2 3 7*2 3 7*2 3 7*2 3 7*2 3 7*2 3 7*2 3 7*2 3 7*2 3 7*2 3 7*2 3
  //   7*2 3 7*2 3 7*2 3 7*2 3 7*2 3 7*2 3 7*2 3 7*2 3 7*2 3 7*2 3 7*2 3 7*2 3 7*2 3 7*2 3 7*2 3 7*2 3 7*2
  //   3 7*2 3 7*2 3 7*2 3 7*2 3 7*2 3 7*2 3 7*2 3 7*2 3 7*2 3 7*2 3 7*2 3 7*2 3 7*2 3 7*2 3 7*2 3 7*2 3
  //   7*2 3 7*2 3 7*2 3 7*2 3 7*2 3 7*2 3 7*2 3 7*2 3 7*2 3 7*2 3 7*2 3 7*2 3 7*2 3 7*2 3 7*2 3 7*2 3 7*2
  //   3 7*2 3 7*2 3 7*2 3 7*2 3 7*2 3 7*2 3 7*2 3 7*2 3 7*2 3 7*2 3 7*2 3 7*2 3 7*2 3 7*2 3 7*2 3 7*2 3
  //   7*2 3 7*2 3 7*2 3 7*2 3 7*2 3 7*2 3 7*2 3 7*2 3 7*2 3 7*2 3 7*2 3 7*2 3 7*2 3 7*2 3 7*2 3 7*2 3 7*2
  //   3 7*2 3 7*2 3 7*2 3 7*2 3 7*2 3 7*2 3 7*2 3 7*2 3 7*2 3 7*2 3 7*2 3 7*2 3 7*2 3 7*2 3 7*2 3 7*2 3
  //   7*2 3 7*2 3 7*2 3 7*2 3 7*2 3 7*2 3 7*2 3 7*2 3 7*2 3 7*2 3 7*2 3 7*2 3 7*2 3 7*2 3 7*2 3 7*2 3 7*2
  //   3 7*2 3 7*2 3 7*2 3 7*2 3 7*2 3 7*2 3 7*2 3 7*2 3 7*2 3 7*2 3 7*2 3 7*2 3 7*2 3 7*2 3 7*2 3 7*2 3
  //   7*2 3 7*2 3 7*2 3 7*2 3 7*2 3 7*2 3 7*2 3 7*2 3 7*2 3 7*2 3 7*2 3 7*2 3 7*2 3 7*2 3 7*2 3 7*2 3 7*2
  //   3 7*2 3 7*2 3 7*2 3 7*2 3 7*2 3 7*2 3 7*2 3 7*2 3 7*2 3 7*2 3 7*2 3 7*2 3 7*2 3 7*2 3 7*2 3 7*2 3
  //   7*2 3 7*2 3 7*2 3 7*2 3 7*2 3 7*2 3 7*2 3 7*2 3 7*2 3 7*2 3 7*2 3 7*2 3 7*2 3 7*2 3 7*2 3 7*2 3 7*2
  //   3 7*2 3 7*2 3 7*2 3 7*2 3 7*2 3 7*2 3 7*2 3 7*2 3 7*2 3 7*2 3 7*2 3 7*2 3 7*2 3 7*2 3 7*2 3 7*2 3
  //   7*2 3 7*2 3 7*2 3 7*2 3 7*2 3 7*2 3 7*2 3 7*2 3 7*2 3 7*2 3 7*2 3 7*2 3 7*2 3 7*2 3 7*2 3 7*2 3 7*2
  //   3 7*2 3 7*2 3 7*2 3 7*2 3 7*2 3 7*2 3 7*2 3 7*2 3 7*2 3 7*2 3 7*2 3 7*2 3 7*2 3 7*2 3 7*2 3 7*2 3
  //   7*2 3 7*2 3 7*2 3 7*2 3 7*2 3 7*2 3 7*2 3 7*2 3 7*2 3 7*2 3 7*2 3 7*2 3 7*2 3 7*2 3 7*2 3 7*2 3 7*2
  //   3 7*2 3 7*2 3 7*2 3 7*2 3 7*2 3 7*2 3 7*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
  //   uCode1
  //   contents of rom_2 (hex, n*v repeats v):
  //   1025*0 10 20 1 2045*0 10 20 1 2045*0 10 20 1 2045*0 10 20 1 2045*0 10 20 1 2045*0 10 20 1 2045*0 10
  //   20 1 2045*0 10 20 1 2045*0 10 20 1 2045*0 10 20 1 2045*0 10 20 1 2045*0 10 20 1 2045*0 10 20 1
  //   2045*0 10 20 1 2045*0 10 20 1 2045*0 10 20 1
  //   SP
  //   Stp
  //   PC
  //   RA
  //   uCode4
  //   uCode3
  //   RB
  //   contents of rom_3 (hex, n*v repeats v):
  //   1 7*2 1 7*2 1 7*2 1 7*2 1 7*2 1 7*2 1 7*2 1 7*2 1 7*2 1 7*2 1 7*2 1 7*2 1 7*2 1 7*2 1 7*2 1 7*2 1
  //   7*2 1 7*2 1 7*2 1 7*2 1 7*2 1 7*2 1 7*2 1 7*2 1 7*2 1 7*2 1 7*2 1 7*2 1 7*2 1 7*2 1 7*2 1 7*2 1 7*2
  //   1 7*2 1 7*2 1 7*2 1 7*2 1 7*2 1 7*2 1 7*2 1 7*2 1 7*2 1 7*2 1 7*2 1 7*2 1 7*2 1 7*2 1 7*2 1 7*2 1
  //   7*2 1 7*2 1 7*2 1 7*2 1 7*2 1 7*2 1 7*2 1 7*2 1 7*2 1 7*2 1 7*2 1 7*2 1 7*2 1 7*2 1 7*2 1 7*2 1 7*2
  //   1 7*2 1 7*2 1 7*2 1 7*2 1 7*2 1 7*2 1 7*2 1 7*2 1 7*2 1 7*2 1 7*2 1 7*2 1 7*2 1 7*2 1 7*2 1 7*2 1
  //   7*2 1 7*2 1 7*2 1 7*2 1 7*2 1 7*2 1 7*2 1 7*2 1 7*2 1 7*2 1 7*2 1 7*2 1 7*2 1 7*2 1 7*2 1 7*2 1 7*2
  //   1 7*2 1 7*2 1 7*2 1 7*2 1 7*2 1 7*2 1 7*2 1 7*2 1 7*2 1 7*2 1 7*2 1 7*2 1 7*2 1 7*2 1 7*2 1 7*2 1
  //   7*2 1 7*2 1 7*2 1 7*2 1 7*2 1 7*2 1 7*2 1 7*2 1 7*2 1 7*2 1 7*2 1 7*2 1 7*2 1 2 2 2 6 2 2 2 1 7*2 1
  //   7*2 1 7*2 1 7*2 1 7*2 1 7*2 1 7*2 1 7*2 1 7*2 1 7*2 1 7*2 1 7*2 1 7*2 1 7*2 1 7*2 1 7*2 1 7*2 1 7*2
  //   1 7*2 1 7*2 1 7*2 1 7*2 1 7*2 1 7*2 1 7*2 1 7*2 1 7*2 1 7*2 1 7*2 1 7*2 1 7*2 1 7*2 1 7*2 1 7*2 1
  //   7*2 1 7*2 1 7*2 1 7*2 1 7*2 1 7*2 1 7*2 1 7*2 1 7*2 1 7*2 1 7*2 1 7*2 1 7*2 1 7*2 1 7*2 1 7*2 1 7*2
  //   1 7*2 1 7*2 1 7*2 1 7*2 1 7*2 1 7*2 1 7*2 1 7*2 1 7*2 1 7*2 1 7*2 1 7*2 1 7*2 1 7*2 1 7*2 1 7*2 1
  //   7*2 1 7*2 1 7*2 1 7*2 1 7*2 1 7*2 1 7*2 1 7*2 1 7*2 1 7*2 1 7*2 1 7*2 1 7*2 1 7*2 1 7*2 1 7*2 1 7*2
  //   1 7*2 1 7*2 1 7*2 1 7*2 1 7*2 1 7*2 1 7*2 1 7*2 1 7*2 1 7*2 1 7*2 1 7*2 1 7*2 1 7*2 1 7*2 1 7*2 1
  //   7*2 1 7*2 1 7*2 1 7*2 1 7*2 1 7*2 1 7*2 1 7*2 1 7*2 1 7*2 1 7*2 1 7*2 1 7*2 1 7*2 1 7*2 1 7*2 1 7*2
  //   1 7*2 1 7*2 1 7*2 1 7*2 1 7*2 1 7*2 1 7*2 1 7*2 1 7*2 1 7*2 1 7*2 1 7*2 1 7*2 1 7*2 1 7*2 1 7*2 1
  //   7*2 1 7*2 1 7*2 1 7*2 1 7*2 1 7*2 1 7*2 1 7*2 1 7*2 1 7*2 1 7*2 1 7*2 1 7*2 1 7*2 1 7*2 1 7*2 1 7*2
  //   1 7*2 1 7*2 1 7*2 1 7*2 1 7*2 1 7*2 1 7*2 1 7*2 1 7*2 1 7*2 1 7*2 1 7*2 1 7*2 1 7*2 1 7*2 1 7*2 1
  //   7*2 1 7*2 1 7*2 1 7*2 1 7*2 1 7*2 1 7*2 1 7*2 1 7*2 1 7*2 1 7*2 1 7*2 1 7*2 1 7*2 1 7*2 1 7*2 1 7*2
  //   1 7*2 1 7*2 1 7*2 1 7*2 1 7*2 1 7*2 1 7*2 1 7*2 1 7*2 1 7*2 1 7*2 1 7*2 1 7*2 1 7*2 1 7*2 1 7*2 1
  //   7*2 1 7*2 1 7*2 1 7*2 1 7*2 1 7*2 1 7*2 1 7*2 1 7*2 1 7*2 1 7*2 1 7*2 1 7*2 1 7*2 1 7*2 1 7*2 1 7*2
  //   1 7*2 1 7*2 1 7*2 1 7*2 1 7*2 1 7*2 1 7*2 1 7*2 1 7*2 1 7*2 1 7*2 1 7*2 1 7*2 1 7*2 1 7*2 1 7*2 1
  //   7*2 1 7*2 1 7*2 1 7*2 1 7*2 1 7*2 1 7*2 1 7*2 1 7*2 1 7*2 1 7*2 1 7*2 1 7*2 1 7*2 1 7*2 1 7*2 1 7*2
  //   1 7*2 1 7*2 1 7*2 1 7*2 1 7*2 1 7*2 1 2 2 2 6 2 2 2 1 7*2 1 7*2 1 7*2 1 7*2 1 7*2 1 7*2 1 7*2 1 7*2
  //   1 7*2 1 7*2 1 7*2 1 7*2 1 7*2 1 7*2 1 7*2 1 7*2 1 7*2 1 7*2 1 7*2 1 7*2 1 7*2 1 7*2 1 7*2 1 7*2 1
  //   7*2 1 7*2 1 7*2 1 7*2 1 7*2 1 7*2 1 7*2 1 7*2 1 7*2 1 7*2 1 7*2 1 7*2 1 7*2 1 7*2 1 7*2 1 7*2 1 7*2
  //   1 7*2 1 7*2 1 7*2 1 7*2 1 7*2 1 7*2 1 7*2 1 7*2 1 7*2 1 7*2 1 7*2 1 7*2 1 7*2 1 7*2 1 7*2 1 7*2 1
  //   7*2 1 7*2 1 7*2 1 7*2 1 7*2 1 7*2 1 7*2 1 7*2 1 7*2 1 7*2 1 7*2 1 7*2 1 7*2 1 7*2 1 7*2 1 7*2 1 7*2
  //   1 7*2 1 7*2 1 7*2 1 7*2 1 7*2 1 7*2 1 7*2 1 7*2 1 7*2 1 7*2 1 7*2 1 7*2 1 7*2 1 7*2 1 7*2 1 7*2 1
  //   7*2 1 7*2 1 7*2 1 7*2 1 7*2 1 7*2 1 7*2 1 7*2 1 7*2 1 7*2 1 7*2 1 7*2 1 7*2 1 7*2 1 7*2 1 7*2 1 7*2
  //   1 7*2 1 7*2 1 7*2 1 7*2 1 7*2 1 7*2 1 7*2 1 7*2 1 7*2 1 7*2 1 7*2 1 7*2 1 7*2 1 7*2 1 7*2 1 7*2 1
  //   7*2 1 7*2 1 7*2 1 7*2 1 7*2 1 7*2 1 7*2 1 7*2 1 7*2 1 7*2 1 7*2 1 7*2 1 7*2 1 7*2 1 7*2 1 7*2 1 7*2
  //   1 7*2 1 7*2 1 7*2 1 7*2 1 7*2 1 7*2 1 7*2 1 7*2 1 7*2 1 7*2 1 7*2 1 7*2 1 7*2 1 7*2 1 7*2 1 7*2 1
  //   7*2 1 7*2 1 7*2 1 7*2 1 7*2 1 7*2 1 7*2 1 7*2 1 7*2 1 7*2 1 7*2 1 7*2 1 7*2 1 7*2 1 7*2 1 7*2 1 7*2
  //   1 7*2 1 7*2 1 7*2 1 7*2 1 7*2 1 7*2 1 7*2 1 7*2 1 7*2 1 7*2 1 7*2 1 7*2 1 7*2 1 7*2 1 7*2 1 7*2 1
  //   7*2 1 7*2 1 7*2 1 7*2 1 7*2 1 7*2 1 7*2 1 7*2 1 7*2 1 7*2 1 7*2 1 7*2 1 7*2 1 7*2 1 7*2 1 7*2 1 7*2
  //   1 7*2 1 7*2 1 7*2 1 7*2 1 7*2 1 7*2 1 7*2 1 7*2 1 7*2 1 7*2 1 7*2 1 7*2 1 7*2 1 7*2 1 7*2 1 7*2 1
  //   7*2 1 7*2 1 7*2 1 7*2 1 7*2 1 7*2 1 7*2 1 7*2 1 7*2 1 7*2 1 7*2 1 7*2 1 7*2 1 7*2 1 7*2 1 7*2 1 7*2
  //   1 7*2 1 7*2 1 7*2 1 7*2 1 7*2 1 7*2 1 7*2 1 7*2 1 7*2 1 7*2 1 7*2 1 7*2 1 7*2 1 7*2 1 7*2 1 7*2 1 2
  //   2 2 6 2 2 2 1 7*2 1 7*2 1 7*2 1 7*2 1 7*2 1 7*2 1 7*2 1 7*2 1 7*2 1 7*2 1 7*2 1 7*2 1 7*2 1 7*2 1
  //   7*2 1 7*2 1 7*2 1 7*2 1 7*2 1 7*2 1 7*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
  //   contents of rom_4 (hex, n*v repeats v):
  //   1025*0 1 1 10 2045*0 1 1 10 2045*0 1 1 10 2045*0 1 1 10 2045*0 1 1 10 2045*0 1 1 10 2045*0 1 1 10
  //   2045*0 1 1 10 2045*0 1 1 10 2045*0 1 1 10 2045*0 1 1 10 2045*0 1 1 10 2045*0 1 1 10 2045*0 1 1 10
  //   2045*0 1 1 10 2045*0 1 1 10 1020*0 80 0 0 0 20 0 0 0 80 0 0 0 20 0 0 0 80 0 0 0 20 0 0 0 80 0 0 0 20
  //   0 0 0 80 0 0 0 20 0 0 0 80 0 0 0 20 0 0 0 80 0 0 0 20 0 0 0 80 0 0 0 20 0 0 0 80 0 0 0 20 0 0 0 80 0
  //   0 0 20 0 0 0 80 0 0 0 20 0 0 0 80 0 0 0 20 0 0 0 80 0 0 0 20 0 0 0 80 0 0 0 20 0 0 0 80 0 0 0 20 0 0
  //   0 80 0 0 0 20 0 0 0 80 0 0 0 20 0 0 0 80 0 0 0 20 0 0 0 80 0 0 0 20 0 0 0 80 0 0 0 20 0 0 0 80 0 0 0
  //   20 0 0 0 80 0 0 0 20 0 0 0 80 0 0 0 20 0 0 0 80 0 0 0 20 0 0 0 80 0 0 0 20 0 0 0 80 0 0 0 20 0 0 0
  //   80 0 0 0 20 0 0 0 80 0 0 0 20 0 0 0 80 0 0 0 20 0 0 0 80 0 0 0 20 0 0 0 80 0 0 0 20 0 0 0 80 0 0 0
  //   20 0 0 0 80 0 0 0 20 0 0 0 80 0 0 0 20 0 0 0 80 0 0 0 20 0 0 0 80 0 0 0 20 0 0 0 80 0 0 0 20 0 0 0
  //   80 0 0 0 20 0 0 0 80 0 0 0 20 0 0 0 80 0 0 0 20 0 0 0 80 0 0 0 20 0 0 0 80 0 0 0 20 0 0 0 80 0 0 0
  //   20 0 0 0 80 0 0 0 20 0 0 0 80 0 0 0 20 0 0 0 80 0 0 0 20 0 0 0 80 0 0 0 20 0 0 0 80 0 0 0 20 0 0 0
  //   80 0 0 0 20 0 0 0 80 0 0 0 20 0 0 0 80 0 0 0 20 0 0 0 80 0 0 0 20 0 0 0 80 0 0 0 20 0 0 0 80 0 0 0
  //   20 0 0 0 80 0 0 0 20 0 0 0 80 0 0 0 20 0 0 0 80 0 0 0 20 0 0 0 80 0 0 0 20 0 0 0 80 0 0 0 20 0 0 0
  //   80 0 0 0 20 0 0 0 80 0 0 0 20 0 0 0 80 0 0 0 20 0 0 0 80 0 0 0 20 0 0 0 80 0 0 0 20 0 0 0 80 0 0 0
  //   20 0 0 0 80 0 0 0 20 0 0 0 80 0 0 0 20 0 0 0 80 0 0 0 20 0 0 0 80 0 0 0 20 0 0 0 80 0 0 0 20 0 0 0
  //   80 0 0 0 20 0 0 0 80 0 0 0 20 0 0 0 80 0 0 0 20 0 0 0 80 0 0 0 20 0 0 0 80 0 0 0 20 0 0 0 80 0 0 0
  //   20 0 0 0 80 0 0 0 20 0 0 0 80 0 0 0 20 0 0 0 80 0 0 0 20 0 0 0 80 0 0 0 20 0 0 0 80 0 0 0 20 0 0 0
  //   80 0 0 0 20 0 0 0 80 0 0 0 20 0 0 0 80 0 0 0 20 0 0 0 80 0 0 0 20 0 0 0 80 0 0 0 20 0 0 0 80 0 0 0
  //   20 0 0 0 80 0 0 0 20 0 0 0 80 0 0 0 20 0 0 0 80 0 0 0 20 0 0 0 80 0 0 0 20 0 0 0 80 0 0 0 20 0 0 0
  //   80 0 0 0 20 0 0 0 80 0 0 0 20 0 0 0 80 0 0 0 20 0 0 0 80 0 0 0 20 0 0 0 80 0 0 0 20 0 0 0 80 0 0 0
  //   20 0 0 0 80 0 0 0 20 0 0 0 80 0 0 0 20 0 0 0 80 0 0 0 20 0 0 0 80 0 0 0 20 0 0 0 80 0 0 0 20 0 0 0
  //   80 0 0 0 20 0 0 0 80 0 0 0 20 0 0 0 80 0 0 0 20 0 0 0 80 0 0 0 20 0 0 0 80 0 0 0 20 0 0 0 80 0 0 0
  //   20 0 0 0 80 0 0 0 20 0 0 0 80 0 0 0 20 0 0 0 80 0 0 0 20 0 0 0 80 0 0 0 20 0 0 0 80 0 0 0 20 0 0 0
  //   80 0 0 0 20 0 0 0 80 0 0 0 20 0 0 0 80 0 0 0 20 0 0 0 80 0 0 0 20 0 0 0 80 0 0 0 20 0 0 0 80 0 0 0
  //   20 0 0 0 80 0 0 0 20 0 0 0 80 0 0 0 20 0 0 0 80 0 0 0 20 0 0 0 80 0 0 0 20 0 0 0 80 0 0 0 20 0 0 0
  //   80 0 0 0 20 0 0 0 80 0 0 0 20 0 0 0 80 0 0 0 20 0 0 0 80 0 0 0 20 0 0 0 80 0 0 0 20 0 0 0 80 0 0 0
  //   20 0 0 0 80 0 0 0 20 0 0 0 80 0 0 0 20 0 0 0 80 0 0 0 20 0 0 0 80 0 0 0 20 0 0 0 80 0 0 0 20 0 0 0
  //   80 0 0 0 20 0 0 0 80 0 0 0 20 0 0 0 80 0 0 0 20 0 0 0 80 0 0 0 20 0 0 0 80 0 0 0 20 0 0 0 80 0 0 0
  //   20 0 0 0 80 0 0 0 20 0 0 0 80 0 0 0 20 0 0 0 80 0 0 0 20 0 0 0 80 0 0 0 20 0 0 0 80 0 0 0 20 0 0 0
  //   80 0 0 0 20 0 0 0 80 0 0 0 20 0 0 0 80 0 0 0 20 0 0 0 80 0 0 0 20 0 0 0 80 0 0 0 20 0 0 0 80 0 0 0
  //   20 0 0 0 80 0 0 0 20 0 0 0 80 0 0 0 20 0 0 0 80 0 0 0 20 0 0 0 80 0 0 0 20 0 0 0 80 0 0 0 20 0 0 0
  //   80 0 0 0 20 0 0 0 80 0 0 0 20 0 0 0 80 0 0 0 20 0 0 0 80 0 0 0 20 0 0 0 80 0 0 0 20 0 0 0 80 0 0 0
  //   20 0 0 0 80 0 0 0 20 0 0 0 80 0 0 0 20 0 0 0 80 0 0 0 20 0 0 0 80 0 0 0 20 0 0 0 80 0 0 0 20 0 0 0
  //   80 0 0 0 20 0 0 0 80 0 0 0 20 0 0 0 80 0 0 0 20 0 0 0 80 0 0 0 20 0 0 0 80 0 0 0 20 0 0 0 80 0 0 0
  //   20 0 0 0 80 0 0 0 20 0 0 0 80 0 0 0 20 0 0 0 80 0 0 0 20 0 0 0 80 0 0 0 20 0 0 0 80 0 0 0 20 0 0 0
  //   80 0 0 0 20 0 0 0 80 0 0 0 20 0 0 0 80 0 0 0 20 0 0 0 80 0 0 0 20 0 0 0 80 0 0 0 20 0 0 0 80 0 0 0
  //   20 0 0 0 80 0 0 0 20 0 0 0 80 0 0 0 20 0 0 0 80 0 0 0 20 0 0 0 80 0 0 0 20 0 0 0 80 0 0 0 20 0 0 0
  //   80 0 0 0 20 0 0 0 80 0 0 0 20 0 0 0 80 0 0 0 20 0 0 0 80 0 0 0 20 0 0 0 80 0 0 0 20 0 0 0 80 0 0 0
  //   20 0 0 0 80 0 0 0 20 0 0 0 80 0 0 0 20 0 0 0 80 0 0 0 20 0 0 0 80 0 0 0 20 0 0 0 80 0 0 0 20 0 0 0
  //   80 0 0 0 20 0 0 0 80 0 0 0 20 0 0 0 80 0 0 0 20 0 0 0 80 0 0 0 20 0 0 0 80 0 0 0 20 0 0 0 80 0 0 0
  //   20 0 0 0 80 0 0 0 20 0 0 0 80 0 0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
  //   DI
  //   RC
  //   SI
  //   RD
  //   uCode5
  //   TMP
  //   contents of rom_5 (hex, n*v repeats v):
  //   5a 7*5f 5a 7*5f 5a 7*5f 5a 7*5f 5a 7*5f 5a 7*5f 5a 7*5f 5a 7*5f 5a 7*5f 5a 7*5f 5a 7*5f 5a 7*5f 5a
  //   7*5f 5a 7*5f 5a 7*5f 5a 7*5f 5a 7*5f 5a 7*5f 5a 7*5f 5a 7*5f 5a 7*5f 5a 7*5f 5a 7*5f 5a 7*5f 5a 7*5f
  //   5a 7*5f 5a 7*5f 5a 7*5f 5a 7*5f 5a 7*5f 5a 7*5f 5a 7*5f 5a 7*5f 5a 7*5f 5a 7*5f 5a 7*5f 5a 7*5f 5a
  //   7*5f 5a 7*5f 5a 7*5f 5a 7*5f 5a 7*5f 5a 7*5f 5a 7*5f 5a 7*5f 5a 7*5f 5a 7*5f 5a 7*5f 5a 7*5f 5a 7*5f
  //   5a 7*5f 5a 7*5f 5a 7*5f 5a 7*5f 5a 7*5f 5a 7*5f 5a 7*5f 5a 7*5f 5a 7*5f 5a 7*5f 5a 7*5f 5a 7*5f 5a
  //   7*5f 5a 7*5f 5a 7*5f 5a 7*5f 5a 7*5f 5a 7*5f 5a 7*5f 5a 7*5f 5a 7*5f 5a 7*5f 5a 7*5f 5a 7*5f 5a 7*5f
  //   5a 7*5f 5a 7*5f 5a 7*5f 5a 7*5f 5a 7*5f 5a 7*5f 5a 7*5f 5a 7*5f 5a 7*5f 5a 7*5f 5a 7*5f 5a 7*5f 5a
  //   7*5f 5a 7*5f 5a 7*5f 5a 7*5f 5a 7*5f 5a 7*5f 5a 7*5f 5a 7*5f 5a 7*5f 5a 7*5f 5a 7*5f 5a 7*5f 5a 7*5f
  //   5a 7*5f 5a 7*5f 5a 7*5f 5a 7*5f 5a 7*5f 5a 7*5f 5a 7*5f 5a 7*5f 5a 7*5f 5a 7*5f 5a 7*5f 5a 7*5f 5a
  //   7*5f 5a 7*5f 5a 7*5f 5a 7*5f 5a 7*5f 5a 7*5f 5a 7*5f 5a 7*5f 5a 7*5f 5a 7*5f 5a 7*5f 5a 7*5f 5a 7*5f
  //   5a 7*5f 5a 7*5f 5a 7*5f 5a 7*5f 5a 7*5f 5a 7*5f 5a 7*5f 5a 7*5f 5a 7*5f 5a 7*5f 5a 7*5f 5a 7*5f 5a
  //   7*5f 5a 7*5f 5a 7*5f 5a 7*5f 5a 7*5f 5a 7*5f 5a 7*5f 5a 7*5f 5a 7*5f 5a 7*5f 5a 7*5f 5a 7*5f 5a 7*5f
  //   5a 7*5f 5a 7*5f 5a 7*5f 5a 7*5f 5a 7*5f 5a 7*5f 5a 7*5f 5a 7*5f 5a 7*5f 5a 7*5f 5a 7*5f 5a 7*5f 5a
  //   7*5f 5a 7*5f 5a 7*5f 5a 7*5f 5a 7*5f 5a 7*5f 5a 7*5f 5a 7*5f 5a 7*5f 5a 7*5f 5a 7*5f 5a 7*5f 5a 7*5f
  //   5a 7*5f 5a 7*5f 5a 7*5f 5a 7*5f 5a 7*5f 5a 7*5f 5a 7*5f 5a 7*5f 5a 7*5f 5a 7*5f 5a 7*5f 5a 7*5f 5a
  //   7*5f 5a 7*5f 5a 7*5f 5a 7*5f 5a 7*5f 5a 7*5f 5a 7*5f 5a 7*5f 5a 7*5f 5a 7*5f 5a 7*5f 5a 7*5f 5a 7*5f
  //   5a 7*5f 5a 7*5f 5a 7*5f 5a 7*5f 5a 7*5f 5a 7*5f 5a 7*5f 5a 7*5f 5a 7*5f 5a 7*5f 5a 7*5f 5a 7*5f 5a
  //   7*5f 5a 7*5f 5a 7*5f 5a 7*5f 5a 7*5f 5a 7*5f 5a 7*5f 5a 7*5f 5a 7*5f 5a 7*5f 5a 7*5f 5a 7*5f 5a 7*5f
  //   5a 7*5f 5a 7*5f 5a 7*5f 5a 7*5f 5a 7*5f 5a 7*5f 5a 7*5f 5a 7*5f 5a 7*5f 5a 7*5f 5a 7*5f 5a 7*5f 5a
  //   7*5f 5a 7*5f 5a 7*5f 5a 7*5f 5a 7*5f 5a 7*5f 5a 7*5f 5a 7*5f 5a 7*5f 5a 7*5f 5a 7*5f 5a 7*5f 5a 7*5f
  //   5a 7*5f 5a 7*5f 5a 7*5f 5a 7*5f 5a 7*5f 5a 7*5f 5a 7*5f 5a 7*5f 5a 7*5f 5a 7*5f 5a 7*5f 5a 7*5f 5a
  //   7*5f 5a 7*5f 5a 7*5f 5a 7*5f 5a 7*5f 5a 7*5f 5a 7*5f 5a 7*5f 5a 7*5f 5a 7*5f 5a 7*5f 5a 7*5f 5a 7*5f
  //   5a 7*5f 5a 7*5f 5a 7*5f 5a 7*5f 5a 7*5f 5a 7*5f 5a 7*5f 5a 7*5f 5a 7*5f 5a 7*5f 5a 7*5f 5a 7*5f 5a
  //   7*5f 5a 7*5f 5a 7*5f 5a 7*5f 5a 7*5f 5a 7*5f 5a 7*5f 5a 7*5f 5a 7*5f 5a 7*5f 5a 7*5f 5a 7*5f 5a 7*5f
  //   5a 7*5f 5a 7*5f 5a 7*5f 5a 7*5f 5a 7*5f 5a 7*5f 5a 7*5f 5a 7*5f 5a 7*5f 5a 7*5f 5a 7*5f 5a 7*5f 5a
  //   7*5f 5a 7*5f 5a 7*5f 5a 7*5f 5a 7*5f 5a 7*5f 5a 7*5f 5a 7*5f 5a 7*5f 5a 7*5f 5a 7*5f 5a 7*5f 5a 7*5f
  //   5a 7*5f 5a 7*5f 5a 7*5f 5a 7*5f 5a 7*5f 5a 7*5f 5a 7*5f 5a 7*5f 5a 7*5f 5a 7*5f 5a 7*5f 5a 7*5f 5a
  //   7*5f 5a 7*5f 5a 7*5f 5a 7*5f 5a 7*5f 5a 7*5f 5a 7*5f 5a 7*5f 5a 7*5f 5a 7*5f 5a 7*5f 5a 7*5f 5a 7*5f
  //   5a 7*5f 5a 7*5f 5a 7*5f 5a 7*5f 5a 7*5f 5a 7*5f 5a 7*5f 5a 7*5f 5a 7*5f 5a 7*5f 5a 7*5f 5a 7*5f 5a
  //   7*5f 5a 7*5f 5a 7*5f 5a 7*5f 5a 7*5f 5a 7*5f 5a 7*5f 5a 7*5f 5a 7*5f 5a 7*5f 5a 7*5f 5a 7*5f 5a 7*5f
  //   5a 7*5f 5a 7*5f 5a 7*5f 5a 7*5f 5a 7*5f 5a 7*5f 5a 7*5f 5a 7*5f 5a 7*5f 5a 7*5f 5a 7*5f 5a 7*5f 5a
  //   7*5f 5a 7*5f 5a 7*5f 5a 7*5f 5a 7*5f 5a 7*5f 5a 7*5f 5a 7*5f 5a 7*5f 5a 7*5f 5a 7*5f 5a 7*5f 5a 7*5f
  //   5a 7*5f 5a 7*5f 5a 7*5f 5a 7*5f 5a 7*5f 5a 7*5f 5a 7*5f 5a 7*5f 5a 7*5f 5a 7*5f 5a 7*5f 5a 7*5f 5a
  //   7*5f 5a 7*5f 5a 7*5f 5a 7*5f 5a 7*5f 5a 7*5f 5a 7*5f 5a 7*5f 5a 7*5f 5a 7*5f 5a 7*5f 5a 7*5f 5a 7*5f
  //   5a 7*5f 5a 7*5f 5a 7*5f 5a 7*5f 5a 7*5f 5a 7*5f 5a 7*5f 5a 7*5f 5a 7*5f 5a 7*5f 5a 7*5f 5a 7*5f 5a
  //   7*5f 5a 7*5f 5a 7*5f 5a 7*5f 5a 7*5f 5a 7*5f 5a 7*5f 5a 7*5f 5a 7*5f 5a 7*5f 5a 7*5f 5a 7*5f 5a 7*5f
  //   5a 7*5f 5a 7*5f 5a 7*5f 5a 7*5f 5a 7*5f 5a 7*5f 5a 7*5f 5a 7*5f 5a 7*5f 5a 7*5f 5a 7*5f 5a 7*5f 5a
  //   7*5f 5a 7*5f 5a 7*5f 5a 7*5f 5a 7*5f 5a 7*5f 5a 7*5f 5a 7*5f 5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
  //   ACC
  //   MAR
  //   F
  //   contents of rom_7 (hex, n*v repeats v):
  //   80
endmodule

module _8bitreg (
  input  Load,
  input  Clock,
  input  [7:0] DataIn,
  input  nCntEna,
  input  Reset,
  input  Up_nDown,
  input  Enable,
  output Zout,
  output [7:0] Dout,
  output [7:0] Dout_2
);

  wire cd4516be_1_ncarryout;

  CD4516BE cd4516be_1 (
    .P0(DataIn[0]), .P1(DataIn[1]), .P2(DataIn[2]), .P3(DataIn[3]), .Reset(Reset), .Preset_Enable(Load),
    .Clock(Clock), .nCarryOut(cd4516be_1_ncarryout), .nCarryIn(nCntEna), .Up_Down(Up_nDown), .Q0(Dout[0]),
    .Q1(Dout[1]), .Q2(Dout[2]), .Q3(Dout[3]));  // open: VCC, VSS
  CD4516BE cd4516be_2 (
    .P0(DataIn[4]), .P1(DataIn[5]), .P2(DataIn[6]), .P3(DataIn[7]), .Reset(Reset), .Preset_Enable(Load),
    .Clock(Clock), .nCarryIn(cd4516be_1_ncarryout), .Up_Down(Up_nDown), .Q0(Dout[4]), .Q1(Dout[5]),
    .Q2(Dout[6]), .Q3(Dout[7]));  // open: nCarryOut, VCC, VSS
  nor nor_1 (Zout, Dout[7], Dout[6], Dout[5], Dout[4], Dout[3], Dout[2], Dout[1], Dout[0]);
  assign Dout_2 = Enable ? Dout : 8'bz;  // Controlled_Buffer controlled_buffer_1

  // Notes on the sheet:
  //   Dout_2: pull=down
  //   74HC4078
endmodule

module _16bitreg (
  input  [15:0] DataIn,
  input  Load,
  input  Clock,
  input  nCntEna,
  input  Up_nDown,
  input  Reset,
  input  Enable,
  output [15:0] Dout,
  output [15:0] Dout_2
);

  wire cd4516be_1_ncarryout, cd4516be_2_ncarryout, cd4516be_3_ncarryout;

  CD4516BE cd4516be_1 (
    .P0(DataIn[0]), .P1(DataIn[1]), .P2(DataIn[2]), .P3(DataIn[3]), .Reset(Reset), .Preset_Enable(Load),
    .Clock(Clock), .nCarryOut(cd4516be_1_ncarryout), .nCarryIn(nCntEna), .Up_Down(Up_nDown), .Q0(Dout[0]),
    .Q1(Dout[1]), .Q2(Dout[2]), .Q3(Dout[3]));  // open: VCC, VSS
  CD4516BE cd4516be_2 (
    .P0(DataIn[4]), .P1(DataIn[5]), .P2(DataIn[6]), .P3(DataIn[7]), .Reset(Reset), .Preset_Enable(Load),
    .Clock(Clock), .nCarryOut(cd4516be_2_ncarryout), .nCarryIn(cd4516be_1_ncarryout), .Up_Down(Up_nDown),
    .Q0(Dout[4]), .Q1(Dout[5]), .Q2(Dout[6]), .Q3(Dout[7]));  // open: VCC, VSS
  CD4516BE cd4516be_3 (
    .P0(DataIn[8]), .P1(DataIn[9]), .P2(DataIn[10]), .P3(DataIn[11]), .Reset(Reset), .Preset_Enable(Load),
    .Clock(Clock), .nCarryOut(cd4516be_3_ncarryout), .nCarryIn(cd4516be_2_ncarryout), .Up_Down(Up_nDown),
    .Q0(Dout[8]), .Q1(Dout[9]), .Q2(Dout[10]), .Q3(Dout[11]));  // open: VCC, VSS
  CD4516BE cd4516be_4 (
    .P0(DataIn[12]), .P1(DataIn[13]), .P2(DataIn[14]), .P3(DataIn[15]), .Reset(Reset), .Preset_Enable(Load),
    .Clock(Clock), .nCarryIn(cd4516be_3_ncarryout), .Up_Down(Up_nDown), .Q0(Dout[12]), .Q1(Dout[13]),
    .Q2(Dout[14]), .Q3(Dout[15]));  // open: nCarryOut, VCC, VSS
  assign Dout_2 = Enable ? Dout : 16'bz;  // Controlled_Buffer controlled_buffer_1

  // Notes on the sheet:
  //   Dout_2: pull=down
endmodule

module HM62256sel (
  input  nWE,
  input  nCE,
  input  nOE,
  output Sel,
  output Load
);

  wire nor_1_out;

  nor nor_1 (nor_1_out, nWE, nCE);
  nor nor_2 (Load, nCE, nOE);
  or or_1 (Sel, nor_1_out, Load);

  // Notes on the sheet:
  //   !WE
  //   !CE
  //   !OE
endmodule

module ROMsel (
  input  MEM_ne,
  input  [15:0] Addr,
  output ROMh,
  output ROMl
);

  wire and_1_out, and_2_out, and_3_out, not_1_out, not_2_out, not_3_out, not_4_out;

  not not_1 (not_1_out, MEM_ne);
  not not_2 (not_2_out, Addr[13]);
  not not_3 (not_3_out, Addr[14]);
  not not_4 (not_4_out, Addr[15]);
  and and_1 (and_1_out, not_3_out, not_4_out);
  and and_2 (and_2_out, Addr[13], and_1_out);
  and and_3 (and_3_out, not_2_out, and_1_out);
  nand nand_1 (ROMh, not_1_out, and_2_out);
  nand nand_2 (ROMl, not_1_out, and_3_out);
endmodule

module Bus1 (
  input  [7:0] in_1,
  input  in_2,
  output [7:0] out_3
);

  wire not_1_out;

  not not_1 (not_1_out, in_2);
  or or_1 (out_3[0], in_1[0], in_2);
  and and_1 (out_3[1], in_1[1], not_1_out);
  and and_2 (out_3[2], in_1[2], not_1_out);
  and and_3 (out_3[3], in_1[3], not_1_out);
  and and_4 (out_3[4], in_1[4], not_1_out);
  and and_5 (out_3[5], in_1[5], not_1_out);
  and and_6 (out_3[6], in_1[6], not_1_out);
  and and_7 (out_3[7], in_1[7], not_1_out);
endmodule

module Interrupt (
  input  INTcatch,
  input  INT,
  input  INTdis,
  input  Rst,
  input  INTena,
  output INTout
);

  wire and_1_out, d_ff_1_qn, or_1_out;

  D_Flip_Flop d_ff_1 (.Qn(d_ff_1_qn), .preset(INTdis), .reset(or_1_out));  // open: clk, D, Q, en
  and and_1 (and_1_out, d_ff_1_qn, INT);
  or or_1 (or_1_out, Rst, INTena);
  D_Flip_Flop d_ff_2 (.clk(INTcatch), .D(and_1_out), .Q(INTout), .reset(Rst));  // open: Qn, preset, en
endmodule
